// Logisim project KEDVAC.circ as structural Verilog: 9 circuits, main circuit main
module main (
  input  On_or_Off,
  output Overflow,
  output [7:0] ld_IC,
  output Overflow_2
);

  wire A____MB, clock, clock_1_out, IC____MA, isNeg, ld_A, ld_B, ld_IC_t, ld_MA, ld_MB, ld_OP, MB____IC,
       MB____MA, not_1_out, plus_1, R, stop_clock, Sub, W, xor_1_out, Zero;
  wire [2:0] register_6_q_2;
  wire [3:0] register_1_q, register_1_q_2, register_3_q, register_3_q_2, register_5_q, register_5_q_2,
       register_6_q, register_7_q, register_7_q_2;
  wire [7:0] controlled_buffer_1_out, controlled_buffer_3_out, controlled_buffer_4_out, Into_A, MB_Split,
       n1_1_out_2, out_OP, ram_1_data;
  wire [7:7] not_2_out;

  Hex_Digit_Display hex_digit_display_1 (.value(register_1_q_2));  // open: dp
  Hex_Digit_Display hex_digit_display_2 (.value(register_1_q));  // open: dp
  Register register_1 (
    .D(controlled_buffer_1_out), .en(ld_MA), .Q({register_1_q_2, register_1_q}), .clk(clock));  // open: clr
  xor xor_1 (xor_1_out, stop_clock, 1'b1);
  Clock clock_1 (.out(clock_1_out));
  and and_1 (clock, xor_1_out, clock_1_out);
  RAM ram_1 (
    .addr({register_1_q_2, register_1_q}), .data(ram_1_data), .sel(On_or_Off), .clk(clock), .ld(not_1_out));  // open: clr
  not not_1 (not_1_out, W);
  assign controlled_buffer_1_out = MB____MA ? {3'b000, MB_Split[4:0]} : 8'bz;  // Controlled_Buffer controlled_buffer_1
  assign controlled_buffer_1_out = IC____MA ? {register_3_q_2, register_3_q} : 8'bz;  // Controlled_Buffer controlled_buffer_2
  Hex_Digit_Display hex_digit_display_3 (.value(out_OP[7:4]));  // open: dp
  assign controlled_buffer_3_out = MB____IC ? {3'b000, MB_Split[4:0]} : 8'bz;  // Controlled_Buffer controlled_buffer_3
  Control control_1 (
    .ld_MB(ld_MB), .in_2(out_OP), .IC__MA(IC____MA), .isNeg(isNeg), .IC_plus_plus(plus_1), .MB__IC(MB____IC),
    .ld_MA(ld_MA), .ld_IC(ld_IC_t), .R(R), .clock(clock), .ld_B(ld_B), .W(W), .ld_OP(ld_OP),
    .MB__MA(MB____MA), .ld_A(ld_A), .stop_clock(stop_clock), .A__MB(A____MB), .zero(Zero), .sub(Sub));
  assign controlled_buffer_4_out = R ? ram_1_data : 8'bz;  // Controlled_Buffer controlled_buffer_4
  assign ram_1_data = W ? MB_Split : 8'bz;  // Controlled_Buffer controlled_buffer_5
  Hex_Digit_Display hex_digit_display_4 (.value(out_OP[3:0]));  // open: dp
  Register register_2 (.D({MB_Split[7:5], {5{1'b0}}}), .en(ld_OP), .Q(out_OP), .clk(clock));  // open: clr
  Hex_Digit_Display hex_digit_display_5 (.value(register_3_q_2));  // open: dp
  Hex_Digit_Display hex_digit_display_6 (.value(MB_Split[7:4]));  // open: dp
  Hex_Digit_Display hex_digit_display_7 (.value(register_3_q));  // open: dp
  _1 u_1_1 (.in_1({register_3_q_2, register_3_q}), .out_2(n1_1_out_2), .Overflow(Overflow_2));
  Register register_3 (
    .D(controlled_buffer_3_out), .en(ld_IC_t), .Q({register_3_q_2, register_3_q}), .clk(clock));  // open: clr
  Hex_Digit_Display hex_digit_display_8 (.value(MB_Split[3:0]));  // open: dp
  Register register_4 (.D(controlled_buffer_4_out), .en(ld_MB), .Q(MB_Split), .clk(clock));  // open: clr
  assign controlled_buffer_3_out = plus_1 ? n1_1_out_2 : 8'bz;  // Controlled_Buffer controlled_buffer_6
  Hex_Digit_Display hex_digit_display_9 (.value(register_5_q_2));  // open: dp
  assign controlled_buffer_4_out = A____MB ? {isNeg, register_6_q_2, register_6_q} : 8'bz;  // Controlled_Buffer controlled_buffer_7
  Hex_Digit_Display hex_digit_display_10 (.value(register_5_q));  // open: dp
  Register register_5 (.D(MB_Split), .en(ld_B), .Q({register_5_q_2, register_5_q}), .clk(clock));  // open: clr
  Hex_Digit_Display hex_digit_display_11 (.value({isNeg, register_6_q_2}));  // open: dp
  Hex_Digit_Display hex_digit_display_12 (.value(register_6_q));  // open: dp
  Register register_6 (.D(Into_A), .en(ld_A), .Q({isNeg, register_6_q_2, register_6_q}), .clk(clock));  // open: clr
  ALU alu_1 (.in_1(Sub), .in_2({register_5_q_2, register_5_q}), .in_3(ld_IC), .out_4(Into_A), .out_5(Overflow));
  assign ld_IC = {isNeg, register_6_q_2, register_6_q} & {8{not_2_out[7]}};  // AND_Gate and_2, 8 bits wide
  not not_2 (not_2_out[7], Zero);
  Hex_Digit_Display hex_digit_display_13 (.value(register_7_q_2));  // open: dp
  Hex_Digit_Display hex_digit_display_14 (.value(register_7_q));  // open: dp
  Register register_7 (.Q({register_7_q_2, register_7_q}));  // open: D, en, clk, clr

  // Other names for the same wires on the sheet: Power = On_or_Off
endmodule

module FullAdder (
  input  A,
  input  B,
  input  Carry_In,
  output out_4,
  output out_5
);

  wire and_1_out, and_2_out, xor_1_out;

  xor xor_1 (xor_1_out, A, B);
  xor xor_2 (out_4, xor_1_out, Carry_In);
  and and_1 (and_1_out, xor_1_out, Carry_In);
  and and_2 (and_2_out, B, A);
  or or_1 (out_5, and_1_out, and_2_out);
endmodule

module _8BitAdder (
  input  A0,
  input  A1,
  input  A2,
  input  A3,
  input  A4,
  input  A5,
  input  A6,
  input  A7,
  input  B0,
  input  B1,
  input  B2,
  input  B3,
  input  B4,
  input  B5,
  input  B6,
  input  B7,
  output [7:0] Output,
  output Overflow
);

  wire fulladder_1_out_5, fulladder_2_out_5, fulladder_3_out_5, fulladder_4_out_5, fulladder_5_out_5,
       fulladder_6_out_5, halfadder_1_out_4;

  HalfAdder halfadder_1 (.in_1(A0), .in_2(B0), .out_3(Output[0]), .out_4(halfadder_1_out_4));
  FullAdder fulladder_1 (.A(halfadder_1_out_4), .B(A1), .Carry_In(B1), .out_4(Output[1]), .out_5(fulladder_1_out_5));
  FullAdder fulladder_2 (.A(fulladder_1_out_5), .B(A2), .Carry_In(B2), .out_4(Output[2]), .out_5(fulladder_2_out_5));
  FullAdder fulladder_3 (.A(fulladder_2_out_5), .B(A3), .Carry_In(B3), .out_4(Output[3]), .out_5(fulladder_3_out_5));
  FullAdder fulladder_4 (.A(fulladder_3_out_5), .B(A4), .Carry_In(B4), .out_4(Output[4]), .out_5(fulladder_4_out_5));
  FullAdder fulladder_5 (.A(fulladder_4_out_5), .B(A5), .Carry_In(B5), .out_4(Output[5]), .out_5(fulladder_5_out_5));
  FullAdder fulladder_6 (.A(fulladder_5_out_5), .B(A6), .Carry_In(B6), .out_4(Output[6]), .out_5(fulladder_6_out_5));
  FullAdder fulladder_7 (.A(fulladder_6_out_5), .B(A7), .Carry_In(B7), .out_4(Output[7]), .out_5(Overflow));
  Hex_Digit_Display hex_digit_display_1 (.value(Output[7:4]));  // open: dp
  Hex_Digit_Display hex_digit_display_2 (.value(Output[3:0]));  // open: dp
endmodule

module HalfAdder (
  input  in_1,
  input  in_2,
  output out_3,
  output out_4
);

  xor xor_1 (out_3, in_1, in_2);
  and and_1 (out_4, in_1, in_2);
endmodule

module ALU (
  input  in_1,
  input  [7:0] in_2,
  input  [7:0] in_3,
  output [7:0] out_4,
  output out_5
);

  wire n8bitadder_1_overflow, n8bitadder_2_overflow, n8bitadder_3_overflow, not_1_out, not_2_out, not_3_out,
       not_4_out, not_5_out, not_6_out, not_7_out, not_8_out, not_9_out, not_10_out, not_11_out, not_12_out,
       or_1_out;
  wire [7:0] controlled_buffer_1_out, controlled_buffer_2_out, controlled_buffer_3_out,
       controlled_buffer_4_out, n8bitadder_1_output, n8bitadder_2_output, n8bitadder_3_output;

  assign controlled_buffer_1_out = in_1 ? in_3 : 8'bz;  // Controlled_Buffer controlled_buffer_1
  assign controlled_buffer_2_out = in_1 ? in_2 : 8'bz;  // Controlled_Buffer controlled_buffer_2
  assign controlled_buffer_3_out = not_1_out ? in_2 : 8'bz;  // Controlled_Buffer controlled_buffer_3
  not not_1 (not_1_out, in_1);
  assign controlled_buffer_4_out = not_2_out ? in_3 : 8'bz;  // Controlled_Buffer controlled_buffer_4
  not not_2 (not_2_out, in_1);
  _8BitAdder u_8bitadder_1 (
    .A0(controlled_buffer_1_out[0]), .A1(controlled_buffer_1_out[1]), .A2(controlled_buffer_1_out[2]),
    .A3(controlled_buffer_1_out[3]), .A4(controlled_buffer_1_out[4]), .A5(controlled_buffer_1_out[5]),
    .A6(controlled_buffer_1_out[6]), .A7(controlled_buffer_1_out[7]), .B0(not_3_out), .B1(not_4_out),
    .B2(not_5_out), .B3(not_6_out), .B4(not_7_out), .B5(not_8_out), .B6(not_9_out), .B7(not_10_out),
    .Output(n8bitadder_1_output), .Overflow(n8bitadder_1_overflow));
  not not_3 (not_3_out, controlled_buffer_2_out[0]);
  not not_4 (not_4_out, controlled_buffer_2_out[1]);
  not not_5 (not_5_out, controlled_buffer_2_out[2]);
  not not_6 (not_6_out, controlled_buffer_2_out[3]);
  not not_7 (not_7_out, controlled_buffer_2_out[4]);
  not not_8 (not_8_out, controlled_buffer_2_out[5]);
  not not_9 (not_9_out, controlled_buffer_2_out[6]);
  not not_10 (not_10_out, controlled_buffer_2_out[7]);
  _8BitAdder u_8bitadder_2 (
    .A0(controlled_buffer_3_out[0]), .A1(controlled_buffer_3_out[1]), .A2(controlled_buffer_3_out[2]),
    .A3(controlled_buffer_3_out[3]), .A4(controlled_buffer_3_out[4]), .A5(controlled_buffer_3_out[5]),
    .A6(controlled_buffer_3_out[6]), .A7(controlled_buffer_3_out[7]), .B0(controlled_buffer_4_out[0]),
    .B1(controlled_buffer_4_out[1]), .B2(controlled_buffer_4_out[2]), .B3(controlled_buffer_4_out[3]),
    .B4(controlled_buffer_4_out[4]), .B5(controlled_buffer_4_out[5]), .B6(controlled_buffer_4_out[6]),
    .B7(controlled_buffer_4_out[7]), .Output(n8bitadder_2_output), .Overflow(n8bitadder_2_overflow));
  _8BitAdder u_8bitadder_3 (
    .A0(1'b1), .A1(1'b0), .A2(1'b0), .A3(1'b0), .A4(1'b0), .A5(1'b0), .A6(1'b0), .A7(1'b0),
    .B0(n8bitadder_1_output[0]), .B1(n8bitadder_1_output[1]), .B2(n8bitadder_1_output[2]),
    .B3(n8bitadder_1_output[3]), .B4(n8bitadder_1_output[4]), .B5(n8bitadder_1_output[5]),
    .B6(n8bitadder_1_output[6]), .B7(n8bitadder_1_output[7]), .Output(n8bitadder_3_output),
    .Overflow(n8bitadder_3_overflow));
  assign out_5 = not_11_out ? n8bitadder_2_overflow : 1'bz;  // Controlled_Buffer controlled_buffer_5
  not not_11 (not_11_out, in_1);
  assign out_4 = in_1 ? n8bitadder_3_output : 8'bz;  // Controlled_Buffer controlled_buffer_6
  assign out_5 = in_1 ? or_1_out : 1'bz;  // Controlled_Buffer controlled_buffer_7
  or or_1 (or_1_out, n8bitadder_3_overflow, n8bitadder_1_overflow);
  assign out_4 = not_12_out ? n8bitadder_2_output : 8'bz;  // Controlled_Buffer controlled_buffer_8
  not not_12 (not_12_out, in_1);

  // Other names for the same wires on the sheet: Sub = in_1
endmodule

module _1 (
  input  [7:0] in_1,
  output [7:0] out_2,
  output Overflow
);

  _8BitAdder u_8bitadder_1 (
    .A0(1'b1), .A1(1'b0), .A2(1'b0), .A3(1'b0), .A4(1'b0), .A5(1'b0), .A6(1'b0), .A7(1'b0), .B0(in_1[0]),
    .B1(in_1[1]), .B2(in_1[2]), .B3(in_1[3]), .B4(in_1[4]), .B5(in_1[5]), .B6(in_1[6]), .B7(in_1[7]),
    .Output(out_2), .Overflow(Overflow));

  // Notes on the sheet:
  //   out_2: pull=down
endmodule

module SwitchBoi (
  input  in_1,
  output out_2,
  output out_3,
  output out_4,
  output out_5
);

  wire t_ff_1_q, t_ff_1_qn, t_ff_2_q;

  T_Flip_Flop t_ff_1 (.clk(in_1), .T(1'b1), .Q(t_ff_1_q), .Qn(t_ff_1_qn));  // open: preset, reset, en
  T_Flip_Flop t_ff_2 (.clk(in_1), .T(t_ff_1_qn), .Q(t_ff_2_q));  // open: Qn, preset, reset, en
  and and_1 (out_2, ~t_ff_1_q, ~t_ff_2_q);  // AND_Gate
  and and_2 (out_3, t_ff_1_q, t_ff_2_q);
  and and_3 (out_4, ~t_ff_1_q, t_ff_2_q);  // AND_Gate
  and and_4 (out_5, t_ff_1_q, ~t_ff_2_q);  // AND_Gate
endmodule

module OpDecoder (
  input  [7:0] in_1,
  output out_2,
  output out_3,
  output out_4,
  output out_5,
  output out_6,
  output out_7,
  output out_8
);

  wire or_1_out, or_2_out, or_3_out, or_4_out, or_5_out, or_6_out, or_7_out;
  wire [7:0] xor_1_out, xor_2_out, xor_3_out, xor_4_out, xor_5_out, xor_6_out, xor_7_out;

  assign xor_1_out = {8{1'b0}} ^ in_1;  // XOR_Gate xor_1, 8 bits wide
  assign xor_2_out = 8'h20 ^ in_1;  // XOR_Gate xor_2, 8 bits wide
  assign xor_3_out = 8'h40 ^ in_1;  // XOR_Gate xor_3, 8 bits wide
  assign xor_4_out = 8'h60 ^ in_1;  // XOR_Gate xor_4, 8 bits wide
  assign xor_5_out = 8'h80 ^ in_1;  // XOR_Gate xor_5, 8 bits wide
  assign xor_6_out = 8'ha0 ^ in_1;  // XOR_Gate xor_6, 8 bits wide
  assign xor_7_out = 8'he0 ^ in_1;  // XOR_Gate xor_7, 8 bits wide
  not not_1 (out_2, or_1_out);
  or or_1 (or_1_out, xor_1_out[0], xor_1_out[1], xor_1_out[2], xor_1_out[3], xor_1_out[4], xor_1_out[5], xor_1_out[6], xor_1_out[7]);
  not not_2 (out_3, or_2_out);
  or or_2 (or_2_out, xor_2_out[0], xor_2_out[1], xor_2_out[2], xor_2_out[3], xor_2_out[4], xor_2_out[5], xor_2_out[6], xor_2_out[7]);
  not not_3 (out_4, or_3_out);
  or or_3 (or_3_out, xor_3_out[0], xor_3_out[1], xor_3_out[2], xor_3_out[3], xor_3_out[4], xor_3_out[5], xor_3_out[6], xor_3_out[7]);
  not not_4 (out_5, or_4_out);
  or or_4 (or_4_out, xor_4_out[0], xor_4_out[1], xor_4_out[2], xor_4_out[3], xor_4_out[4], xor_4_out[5], xor_4_out[6], xor_4_out[7]);
  not not_5 (out_6, or_5_out);
  or or_5 (or_5_out, xor_5_out[0], xor_5_out[1], xor_5_out[2], xor_5_out[3], xor_5_out[4], xor_5_out[5], xor_5_out[6], xor_5_out[7]);
  not not_6 (out_7, or_6_out);
  or or_6 (or_6_out, xor_6_out[0], xor_6_out[1], xor_6_out[2], xor_6_out[3], xor_6_out[4], xor_6_out[5], xor_6_out[6], xor_6_out[7]);
  not not_7 (out_8, or_7_out);
  or or_7 (or_7_out, xor_7_out[0], xor_7_out[1], xor_7_out[2], xor_7_out[3], xor_7_out[4], xor_7_out[5], xor_7_out[6], xor_7_out[7]);
endmodule

module Control (
  input  clock,
  input  [7:0] in_2,
  input  isNeg,
  output R,
  output ld_MB,
  output ld_B,
  output IC__MA,
  output W,
  output IC_plus_plus,
  output ld_OP,
  output MB__MA,
  output MB__IC,
  output ld_A,
  output ld_MA,
  output zero,
  output stop_clock,
  output ld_IC,
  output sub,
  output A__MB
);

  wire add_Signal, and_2_out, and_3_out, and_4_out, and_13_out, and_14_out, and_15_out, and_16_out,
       and_17_out, and_18_out, and_20_out, and_21_out, b_Signal, bneg_Signal, cPrime, halt_Signal, isPrime,
       ld_Signal, or_1_out, or_2_out, or_3_out, or_4_out, or_6_out, or_7_out, R_t, st_Signal, sub_Signal, t0,
       t0_ldMB, t1, t2, t2_IC_plus_plus, t2_ldIC, t2_ldIC_bneg, t2_prime_IC_plus_plus, t3, t3_IC__MA,
       t3_prime_IC__MA;

  SwitchBoi switchboi_1 (.out_2(t0), .out_3(t1), .out_4(t2), .out_5(t3), .in_1(clock));
  OpDecoder opdecoder_1 (
    .in_1(in_2), .out_2(ld_Signal), .out_3(sub_Signal), .out_4(add_Signal), .out_5(st_Signal),
    .out_6(b_Signal), .out_7(bneg_Signal), .out_8(halt_Signal));
  T_Flip_Flop t_ff_1 (.clk(clock), .T(cPrime), .Q(isPrime));  // open: Qn, preset, reset, en
  and and_1 (ld_OP, t1, ~isPrime);  // AND_Gate
  and and_2 (and_2_out, isPrime, t1);
  and and_3 (and_3_out, t3, ~isPrime);  // AND_Gate
  and and_4 (and_4_out, isPrime, t3);
  and and_5 (zero, and_2_out, ld_Signal);
  and and_6 (sub, and_2_out, sub_Signal);
  and and_7 (A__MB, and_3_out, st_Signal);
  or or_1 (or_1_out, b_Signal, bneg_Signal);
  and and_8 (ld_A, and_2_out, or_2_out);
  or or_2 (or_2_out, ld_Signal, sub_Signal, add_Signal);
  and and_9 (R_t, and_3_out, or_3_out);
  or or_3 (or_3_out, ld_Signal, sub_Signal, add_Signal);
  and and_10 (t3_IC__MA, and_3_out, or_1_out);
  and and_11 (t3_prime_IC__MA, and_4_out, or_4_out);
  or or_4 (or_4_out, ld_Signal, sub_Signal, add_Signal, st_Signal);
  or or_5 (cPrime, R_t, A__MB, t3_prime_IC__MA);
  and and_12 (t0_ldMB, t0, ~isPrime);  // AND_Gate
  and and_13 (and_13_out, isPrime, t0);
  and and_14 (and_14_out, t2, ~isPrime);  // AND_Gate
  and and_15 (and_15_out, isPrime, t2);
  and and_16 (and_16_out, and_13_out, ld_Signal);
  and and_17 (and_17_out, and_13_out, sub_Signal);
  and and_18 (and_18_out, and_13_out, add_Signal);
  and and_19 (W, and_13_out, st_Signal);
  and and_20 (and_20_out, and_14_out, isNeg);
  and and_21 (and_21_out, and_14_out, ~isNeg);  // AND_Gate
  or or_6 (or_6_out, ld_Signal, sub_Signal, add_Signal, st_Signal);
  or or_7 (or_7_out, ld_Signal, sub_Signal, add_Signal, st_Signal);
  or or_8 (ld_B, and_16_out, and_17_out, and_18_out);
  and and_22 (MB__MA, and_14_out, or_6_out);
  and and_23 (t2_ldIC, and_14_out, b_Signal);
  and and_24 (stop_clock, halt_Signal, and_14_out);
  and and_25 (t2_ldIC_bneg, and_20_out, bneg_Signal);
  and and_26 (t2_IC_plus_plus, and_21_out, bneg_Signal);
  and and_27 (t2_prime_IC_plus_plus, and_15_out, or_7_out);
  or or_9 (R, t0_ldMB, R_t);
  or or_10 (ld_MB, R_t, A__MB, t0_ldMB);
  or or_11 (IC__MA, t3_IC__MA, t3_prime_IC__MA);
  or or_12 (IC_plus_plus, t2_prime_IC_plus_plus, t2_IC_plus_plus);
  or or_13 (MB__IC, t2_ldIC, t2_ldIC_bneg);
  or or_14 (ld_MA, MB__MA, t3_prime_IC__MA, t3_IC__MA);
  or or_15 (ld_IC, t2_prime_IC_plus_plus, t2_ldIC_bneg, t2_ldIC, t2_IC_plus_plus);

  // Other names for the same wires on the sheet: t2_MB__IC = t2_ldIC; t2_MB__IC_bneg = t2_ldIC_bneg;
  //   t2_ldIC_bneg_2 = t2_IC_plus_plus; t2_ldMA = MB__MA; t2_prime_ldIC = t2_prime_IC_plus_plus; t3_ldMA = t3_IC__MA;
  //   t3_ldMB_other = R_t; t3_ldMB_st = A__MB; t3_prime_ldMA = t3_prime_IC__MA
endmodule
