// Logisim project Multiplexers and Demultiplexers.circ as structural Verilog: 2 circuits, main circuit Multiplexer
module Multiplexer (
  input  in_1,
  input  in_2,
  input  in_3,
  input  in_4,
  input  in_5,
  input  in_6,
  output out_7
);

  wire and_1_out, and_2_out, and_3_out, and_4_out;

  and and_1 (and_1_out, in_2, in_1, in_3);
  and and_2 (and_2_out, ~in_2, in_1, in_4);  // AND_Gate
  and and_3 (and_3_out, in_2, ~in_1, in_5);  // AND_Gate
  and and_4 (and_4_out, ~in_2, ~in_1, in_6);  // AND_Gate
  or or_1 (out_7, and_1_out, and_2_out, and_3_out, and_4_out);
endmodule

module Demultiplexer (
  input  in_1,
  input  in_2,
  input  in_3,
  output out_4,
  output out_5,
  output out_6,
  output out_7
);

  and and_1 (out_4, in_2, in_1, in_3);
  and and_2 (out_5, ~in_2, in_1, in_3);  // AND_Gate
  and and_3 (out_6, in_2, ~in_1, in_3);  // AND_Gate
  and and_4 (out_7, ~in_2, ~in_1, in_3);  // AND_Gate
endmodule
